// Logisim project processador_Bruno.circ as structural Verilog
module Add_4 (
  input  [3:0] B,
  input  [3:0] A,
  input  Vem_1,
  output Vai_1,
  output [3:0] S
);

  wire add_1_2_vai_1, add_1_3_vai_1, add_1_4_vai_1;

  add_1 add_1_1 (.s(S[3]), .vai_1(Vai_1), .A(A[3]), .B(B[3]), .Vem_1(add_1_3_vai_1));
  add_1 add_1_2 (.s(S[1]), .vai_1(add_1_2_vai_1), .A(A[1]), .B(B[1]), .Vem_1(add_1_4_vai_1));
  add_1 add_1_3 (.s(S[2]), .vai_1(add_1_3_vai_1), .A(A[2]), .B(B[2]), .Vem_1(add_1_2_vai_1));
  add_1 add_1_4 (.s(S[0]), .vai_1(add_1_4_vai_1), .A(A[0]), .B(B[0]), .Vem_1(Vem_1));
endmodule

module add_1 (
  input  A,
  input  B,
  input  Vem_1,
  output s,
  output vai_1
);

  wire and_1_out, and_2_out, or_1_out, xor_1_out;

  xor xor_1 (xor_1_out, A, B);
  or or_1 (or_1_out, B, Vem_1);
  and and_1 (and_1_out, B, Vem_1);
  xor xor_2 (s, xor_1_out, Vem_1);
  and and_2 (and_2_out, or_1_out, A);
  or or_2 (vai_1, and_2_out, and_1_out);
endmodule

module Sub_1 (
  input  A,
  input  B,
  input  Vem_1,
  output s,
  output vai_1
);

  wire and_1_out, and_2_out, not_1_out, or_1_out, xor_1_out;

  not not_1 (not_1_out, A);
  xor xor_1 (xor_1_out, A, B);
  or or_1 (or_1_out, B, Vem_1);
  and and_1 (and_1_out, B, Vem_1);
  xor xor_2 (s, xor_1_out, Vem_1);
  and and_2 (and_2_out, or_1_out, not_1_out);
  or or_2 (vai_1, and_2_out, and_1_out);
endmodule

module Sub_4 (
  input  [3:0] B,
  input  [3:0] A,
  input  Vem_1,
  output Vai_1,
  output [3:0] S
);

  wire sub_1_2_vai_1, sub_1_3_vai_1, sub_1_4_vai_1;

  Sub_1 sub_1_1 (.A(B[3]), .B(A[3]), .Vem_1(sub_1_2_vai_1), .s(S[3]), .vai_1(Vai_1));
  Sub_1 sub_1_2 (.A(B[2]), .B(A[2]), .Vem_1(sub_1_3_vai_1), .s(S[2]), .vai_1(sub_1_2_vai_1));
  Sub_1 sub_1_3 (.A(B[1]), .B(A[1]), .Vem_1(sub_1_4_vai_1), .s(S[1]), .vai_1(sub_1_3_vai_1));
  Sub_1 sub_1_4 (.A(B[0]), .B(A[0]), .Vem_1(Vem_1), .s(S[0]), .vai_1(sub_1_4_vai_1));
endmodule
